// Logisim project control_logic.circ as structural Verilog: 1 circuit, main circuit control_logic
module control_logic (
  input  [31:0] inst,
  input  BrEq,
  input  BrLt,
  output PCSel,
  output RegWEn,
  output [2:0] ImmSel,
  output BrUn,
  output ASel,
  output BSel,
  output [3:0] ALUSel,
  output MemRW,
  output [1:0] WBSel,
  output CSRSel,
  output CSRWen,
  output lb,
  output lh,
  output sb,
  output sh
);

  wire ALU_out, and0_out, and_1_out, and_2_out, and_3_out, and_9_out, and_10_out, B, beq_out, bge_out,
       bgeu_out, blt_out, bltu_out, bne_out, comparator_1_lt, comparator_22_eq, F3e0, F3e1, F3e2, F3e3, F3e4,
       F3e5, F3e6, F3e7, F7e0, F7e1, F7e20, I, I03, I13, I67, mul0_out, mulh0_out, mulhu0_out, not_1_out,
       not_2_out, not_3_out, or0_out, or_1_out, or_2_out, PCadd4_out, R, sll0_out, slt0_out, sra0_out,
       srl0_out, sub0_out, U, U17, U37, UJ, xor0_out;
  wire [1:0] multiplexer_26_out, multiplexer_27_out;
  wire [2:0] multiplexer_19_out, multiplexer_21_out, multiplexer_22_out, multiplexer_23_out;
  wire [3:0] multiplexer_1_out, multiplexer_2_out, multiplexer_3_out, multiplexer_4_out, multiplexer_5_out,
       multiplexer_6_out, multiplexer_7_out, multiplexer_8_out, multiplexer_9_out, multiplexer_10_out,
       multiplexer_11_out, multiplexer_12_out, multiplexer_13_out, multiplexer_14_out, multiplexer_15_out,
       multiplexer_16_out, multiplexer_18_out, multiplexer_20_out, multiplexer_25_out;

  Multiplexer #(.enable("false"), .width(4)) multiplexer_1 (
    .in0(4'b0000), .in1(4'b0001), .out(multiplexer_1_out), .sel(and0_out));
  and and0 (and0_out, F3e7, F7e0);
  Multiplexer #(.enable("false"), .width(4)) multiplexer_2 (
    .in0(multiplexer_25_out), .in1(4'b0001), .out(multiplexer_2_out), .sel(F3e7));
  Multiplexer #(.enable("false"), .width(4)) multiplexer_3 (
    .in0(multiplexer_1_out), .in1(4'b0010), .out(multiplexer_3_out), .sel(or0_out));
  and or0 (or0_out, F3e6, F7e0);
  Multiplexer #(.enable("false"), .width(4)) multiplexer_4 (
    .in0(multiplexer_2_out), .in1(4'b0010), .out(multiplexer_4_out), .sel(F3e6));
  Comparator #(.width(3)) comparator_1 (.a(inst[14:12]), .b(3'b000), .eq(F3e0), .lt(comparator_1_lt));  // open: gt
  Comparator #(.width(3)) comparator_2 (.a(inst[14:12]), .b(3'b001), .eq(F3e1));  // open: gt, lt
  Comparator #(.width(3)) comparator_3 (.a(inst[14:12]), .b(3'b010), .eq(F3e2));  // open: gt, lt
  Comparator #(.width(3)) comparator_4 (.a(inst[14:12]), .b(3'b011), .eq(F3e3));  // open: gt, lt
  Comparator #(.width(3)) comparator_5 (.a(inst[14:12]), .b(3'b100), .eq(F3e4));  // open: gt, lt
  Comparator #(.width(3)) comparator_6 (.a(inst[14:12]), .b(3'b101), .eq(F3e5));  // open: gt, lt
  Comparator #(.width(3)) comparator_7 (.a(inst[14:12]), .b(3'b110), .eq(F3e6));  // open: gt, lt
  Comparator #(.width(3)) comparator_8 (.a(inst[14:12]), .b(3'b111), .eq(F3e7));  // open: gt, lt
  Multiplexer #(.enable("false"), .width(4)) multiplexer_5 (
    .in0(multiplexer_3_out), .in1(4'b0011), .out(multiplexer_5_out), .sel(xor0_out));
  and xor0 (xor0_out, F3e4, F7e0);
  Multiplexer #(.enable("false"), .width(4)) multiplexer_6 (
    .in0(multiplexer_4_out), .in1(4'b0011), .out(multiplexer_6_out), .sel(F3e4));
  Multiplexer #(.enable("false"), .width(4)) multiplexer_7 (
    .in0(multiplexer_5_out), .in1(4'b0100), .out(multiplexer_7_out), .sel(srl0_out));
  and srl0 (srl0_out, F3e5, F7e0);
  Multiplexer #(.enable("false"), .width(4)) multiplexer_8 (
    .in0(multiplexer_6_out), .in1(4'b0100), .out(multiplexer_8_out), .sel(and_1_out));
  and and_1 (and_1_out, F3e5, F7e0);
  Comparator #(.width(7)) comparator_9 (.a(inst[31:25]), .b({7{1'b0}}), .eq(F7e0));  // open: gt, lt
  Comparator #(.width(7)) comparator_10 (.a(inst[31:25]), .b(7'b0000001), .eq(F7e1));  // open: gt, lt
  Comparator #(.width(7)) comparator_11 (.a(inst[31:25]), .b(7'b0100000), .eq(F7e20));  // open: gt, lt
  Comparator #(.width(7)) comparator_12 (.a(inst[6:0]), .b(7'b1100011), .eq(B));  // open: gt, lt
  Comparator #(.width(7)) comparator_13 (.a(inst[6:0]), .b(7'b0100011), .eq(MemRW));  // open: gt, lt
  Comparator #(.width(7)) comparator_14 (.a(inst[6:0]), .b(7'b0010011), .eq(I13));  // open: gt, lt
  Comparator #(.width(7)) comparator_15 (.a(inst[6:0]), .b(7'b0000011), .eq(I03));  // open: gt, lt
  Multiplexer #(.enable("false"), .width(4)) multiplexer_9 (
    .in0(multiplexer_7_out), .in1(4'b0101), .out(multiplexer_9_out), .sel(sra0_out));
  and sra0 (sra0_out, F3e5, F7e20);
  Multiplexer #(.enable("false"), .width(4)) multiplexer_10 (
    .in0(multiplexer_8_out), .in1(4'b0101), .out(multiplexer_10_out), .sel(and_2_out));
  and and_2 (and_2_out, F3e5, F7e20);
  Multiplexer #(.enable("false"), .width(4)) multiplexer_11 (
    .in0(multiplexer_9_out), .in1(4'b0110), .out(multiplexer_11_out), .sel(sll0_out));
  and sll0 (sll0_out, F3e1, F7e0);
  Multiplexer #(.enable("false"), .width(4)) multiplexer_12 (
    .in0(multiplexer_10_out), .in1(4'b0110), .out(multiplexer_12_out), .sel(and_3_out));
  and and_3 (and_3_out, F3e1, F7e0);
  Multiplexer #(.enable("false"), .width(4)) multiplexer_13 (
    .in0(multiplexer_11_out), .in1(4'b0111), .out(multiplexer_13_out), .sel(slt0_out));
  and slt0 (slt0_out, F3e2, F7e0);
  Multiplexer #(.enable("false"), .width(4)) multiplexer_14 (
    .in0(multiplexer_12_out), .in1(4'b0111), .out(multiplexer_14_out), .sel(F3e2));
  Comparator #(.width(7)) comparator_16 (.a(inst[6:0]), .b(7'b0110011), .eq(R));  // open: gt, lt
  Comparator #(.width(7)) comparator_17 (.a(inst[6:0]), .b(7'b1110011), .eq(CSRWen));  // open: gt, lt
  Comparator #(.width(7)) comparator_18 (.a(inst[6:0]), .b(7'b1100111), .eq(I67));  // open: gt, lt
  Comparator #(.width(7)) comparator_19 (.a(inst[6:0]), .b(7'b1101111), .eq(UJ));  // open: gt, lt
  Comparator #(.width(7)) comparator_20 (.a(inst[6:0]), .b(7'b0110111), .eq(U37));  // open: gt, lt
  Comparator #(.width(7)) comparator_21 (.a(inst[6:0]), .b(7'b0010111), .eq(U17));  // open: gt, lt
  Multiplexer #(.enable("false"), .width(4)) multiplexer_15 (
    .in0(multiplexer_13_out), .in1(4'b1010), .out(multiplexer_15_out), .sel(mul0_out));
  and mul0 (mul0_out, F3e0, F7e1);
  Multiplexer #(.enable("false"), .width(4)) multiplexer_16 (
    .in0(multiplexer_15_out), .in1(4'b1011), .out(multiplexer_16_out), .sel(mulhu0_out));
  and mulhu0 (mulhu0_out, F3e3, F7e1);
  Multiplexer #(.enable("false"), .width(4)) multiplexer_17 (
    .in0(4'b0000), .in1(multiplexer_14_out), .out(ALUSel), .sel(or_1_out));
  or or_1 (or_1_out, I13, R);
  Comparator #(.width(7)) comparator_22 (.a(inst[6:0]), .b(7'b1100011), .eq(comparator_22_eq));  // open: gt, lt
  not not_1 (not_1_out, BrEq);
  not not_2 (not_2_out, BrLt);
  not not_3 (not_3_out, BrLt);
  Multiplexer #(.enable("false"), .width(4)) multiplexer_18 (
    .in0(multiplexer_16_out), .in1(4'b1100), .out(multiplexer_18_out), .sel(sub0_out));
  and sub0 (sub0_out, F3e0, F7e20);
  Multiplexer #(.enable("false"), .width(3)) multiplexer_19 (
    .in0(3'b000), .in1(3'b001), .out(multiplexer_19_out), .sel(MemRW));
  and beq (beq_out, comparator_22_eq, BrEq, F3e0);
  and bne (bne_out, B, not_1_out, F3e1);
  and blt (blt_out, B, BrLt, F3e4);
  and bge (bge_out, B, not_2_out, F3e5);
  and bltu (bltu_out, B, BrLt, F3e6);
  and bgeu (bgeu_out, B, not_3_out, F3e7);
  Multiplexer #(.enable("false"), .width(4)) multiplexer_20 (
    .in0(multiplexer_18_out), .in1(4'b1110), .out(multiplexer_20_out), .sel(mulh0_out));
  and mulh0 (mulh0_out, F3e1, F7e1);
  Multiplexer #(.enable("false"), .width(3)) multiplexer_21 (
    .in0(multiplexer_19_out), .in1(3'b010), .out(multiplexer_21_out), .sel(B));
  Multiplexer #(.enable("false"), .width(3)) multiplexer_22 (
    .in0(multiplexer_21_out), .in1(3'b011), .out(multiplexer_22_out), .sel(U));
  or or_2 (or_2_out, beq_out, bne_out, blt_out, bge_out, bltu_out, bgeu_out);
  Multiplexer #(.enable("false"), .width(3)) multiplexer_23 (
    .in0(multiplexer_22_out), .in1(3'b100), .out(multiplexer_23_out), .sel(UJ));
  Multiplexer #(.enable("false"), .width(3)) multiplexer_24 (
    .in0(multiplexer_23_out), .in1(3'b101), .out(ImmSel), .sel(CSRSel));
  Multiplexer #(.enable("false"), .width(4)) multiplexer_25 (
    .in0(4'b0000), .in1(multiplexer_20_out), .out(multiplexer_25_out), .sel(R));
  or or_3 (PCSel, or_2_out, UJ, I67);
  and and_4 (CSRSel, CSRWen, F3e5);
  or or_4 (ASel, B, U17, UJ);
  or or_5 (BSel, I03, I67, MemRW, B, U, UJ, I13);
  and and_5 (lb, I03, F3e0);
  and and_6 (lh, I03, F3e1);
  and and_7 (sb, MemRW, F3e0);
  and and_8 (sh, MemRW, F3e1);
  and and_9 (and_9_out, B, F3e6);
  and and_10 (and_10_out, B, F3e7);
  or or_6 (U, U37, U17);
  or or_7 (BrUn, and_9_out, and_10_out);
  or or_8 (RegWEn, R, I, U, UJ);
  or or_9 (I, I13, I03, I67);
  Multiplexer #(.enable("false"), .width(2)) multiplexer_26 (
    .in0(2'b00), .in1(2'b01), .out(multiplexer_26_out), .sel(ALU_out));
  or ALU (ALU_out, R, I13, U17);
  Multiplexer #(.enable("false"), .width(2)) multiplexer_27 (
    .in0(multiplexer_26_out), .in1(2'b10), .out(multiplexer_27_out), .sel(PCadd4_out));
  or PCadd4 (PCadd4_out, UJ, I67);
  Multiplexer #(.enable("false"), .width(2)) multiplexer_28 (
    .in0(multiplexer_27_out), .in1(2'b11), .out(WBSel), .sel(U37));

  // Other names for the same wires on the sheet: csrwi = CSRSel; I73 = CSRWen; opcode[6:0] = inst[6:0];
  //   rd[4:0] = inst[11:7]; funct3[2:0] = inst[14:12]; rs1[4:0] = inst[19:15]; rs2[4:0] = inst[24:20];
  //   funct7[6:0] = inst[31:25]; S = MemRW

  // Notes on the sheet:
  //   INPUTS to your circuit
  //   DON'T CHANGE THE LOCATIONS OF THE INPUTS AND OUTPUTS!
  //   OUTPUT from your circuit
  //   I=0, S=1, SB=2, U=3, UJ=4, CSRW=5
  //   PCSel
  //   AB_SELECT
  //   LS_BH
  //   ImmSel MemRW CSRSel BrUn
  //   WBSel
  //   imm
  //   RegWEn
endmodule
