// Logisim project cpu.circ as structural Verilog: 1 circuit, main circuit cpu
module cpu (
  input  clk,
  input  [31:0] INSTRUCTION,
  input  [31:0] READ_DATA,
  output [31:0] WRITE_ADDRESS,
  output [31:0] PROGRAM_COUNTER,
  output [31:0] ra,
  output [31:0] sp,
  output [31:0] t0,
  output [31:0] t1,
  output [31:0] t2,
  output [31:0] s0,
  output [31:0] s1,
  output [31:0] a0,
  output [31:0] tohost,
  output [3:0] WRITE_ENABLE,
  output [31:0] WRITE_DATA
);

  wire ASel, BrEq, BrLt, BrUn, BSel, CSRSel, CSRWen, lb, lh, MemRW, PCSel, RegWEn, sb, sh;
  wire [1:0] WBSel;
  wire [2:0] control_logic_1_immsel;
  wire [3:0] ALUSel, multiplexer_6_out, multiplexer_8_out;
  wire [31:0] adder_1_out, bit_extender_1_out, bit_extender_2_out, DataA, imm, INSTRUCTION2,
       multiplexer_1_out, multiplexer_2_out, multiplexer_3_out, multiplexer_4_out, multiplexer_5_out,
       multiplexer_7_out, PCadd4, PROGRAM_COUNTER2, READ_DATA2, WB_Data;

  Adder #(.width(32)) adder_1 (.a(PROGRAM_COUNTER), .b(32'h4), .out(adder_1_out));  // open: cin, cout
  Multiplexer #(.enable("false"), .width(32)) multiplexer_1 (
    .in0(INSTRUCTION), .in1(32'h13), .out(multiplexer_1_out), .sel(PCSel));
  Multiplexer #(.enable("false"), .width(32)) multiplexer_2 (
    .in0(adder_1_out), .in1(WRITE_ADDRESS), .out(multiplexer_2_out), .sel(PCSel));
  Register #(.width(32)) pipePC (.D(PROGRAM_COUNTER), .clk(clk), .Q(PROGRAM_COUNTER2));  // open: en, clr
  Register #(.width(32)) pipeInst (.D(multiplexer_1_out), .clk(clk), .Q(INSTRUCTION2));  // open: en, clr
  Register #(.width(32)) PC (.D(multiplexer_2_out), .clk(clk), .Q(PROGRAM_COUNTER));  // open: en, clr
  control_logic control_logic_1 (
    .CSRWen(CSRWen), .lb(lb), .lh(lh), .sb(sb), .sh(sh), .PCSel(PCSel), .RegWEn(RegWEn),
    .ImmSel(control_logic_1_immsel), .BrUn(BrUn), .ASel(ASel), .BSel(BSel), .ALUSel(ALUSel), .MemRW(MemRW),
    .WBSel(WBSel), .CSRSel(CSRSel), .inst(INSTRUCTION2), .BrEq(BrEq), .BrLt(BrLt));
  regfile regfile_1 (
    .rs1(INSTRUCTION2[19:15]), .rs2(INSTRUCTION2[24:20]), .rd(INSTRUCTION2[11:7]), .Write_Data(WB_Data),
    .RegWEn(RegWEn), .clk(clk), .ra(ra), .sp(sp), .t0(t0), .t1(t1), .t2(t2), .s0(s0), .s1(s1), .a0(a0),
    .Read_Data_1(DataA), .Read_Data_2(WRITE_DATA));
  branch_comp branch_comp_1 (.rs1(DataA), .rs2(WRITE_DATA), .BrUn(BrUn), .BrEq(BrEq), .BrLt(BrLt));
  imm_gen imm_gen_1 (.inst(INSTRUCTION2), .ImmSel(control_logic_1_immsel), .imm(imm));
  Multiplexer #(.enable("false"), .width(32)) multiplexer_3 (
    .in0(DataA), .in1(PROGRAM_COUNTER2), .out(multiplexer_3_out), .sel(ASel));
  Multiplexer #(.enable("false"), .width(32)) multiplexer_4 (
    .in0(WRITE_DATA), .in1(imm), .out(multiplexer_4_out), .sel(BSel));
  Multiplexer #(.enable("false"), .width(32)) multiplexer_5 (
    .in0(DataA), .in1(imm), .out(multiplexer_5_out), .sel(CSRSel));
  alu alu_1 (.Result(WRITE_ADDRESS), .A(multiplexer_3_out), .B(multiplexer_4_out), .ALUSel(ALUSel));
  csr csr_1 (.CSR_address(12'h51e), .CSR_din(multiplexer_5_out), .CSR_WE(CSRWen), .clk(clk), .tohost(tohost));
  Adder #(.width(32)) adder_2 (.a(PROGRAM_COUNTER2), .b(32'h4), .out(PCadd4));  // open: cin, cout
  Multiplexer #(.enable("false"), .width(4)) multiplexer_6 (
    .in0(4'b1111), .in1(4'b0011), .out(multiplexer_6_out), .sel(sh));
  Multiplexer #(.enable("false"), .width(32)) multiplexer_7 (
    .in0(READ_DATA), .in1(bit_extender_1_out), .out(multiplexer_7_out), .sel(lh));
  assign bit_extender_1_out = {{16{READ_DATA[15]}}, READ_DATA[15:0]};  // Bit_Extender bit_extender_1
  Multiplexer #(.enable("false"), .width(4)) multiplexer_8 (
    .in0(multiplexer_6_out), .in1(4'b0001), .out(multiplexer_8_out), .sel(sb));
  Multiplexer #(.enable("false"), .width(4)) multiplexer_9 (
    .in0(4'b0000), .in1(multiplexer_8_out), .out(WRITE_ENABLE), .sel(MemRW));
  Multiplexer #(.enable("false"), .select(2), .width(32)) multiplexer_10 (
    .in0(READ_DATA2), .in1(WRITE_ADDRESS), .in2(PCadd4), .in3(imm), .out(WB_Data), .sel(WBSel));
  Multiplexer #(.enable("false"), .width(32)) multiplexer_11 (
    .in0(multiplexer_7_out), .in1(bit_extender_2_out), .out(READ_DATA2), .sel(lb));
  assign bit_extender_2_out = {{24{READ_DATA[7]}}, READ_DATA[7:0]};  // Bit_Extender bit_extender_2

  // Other names for the same wires on the sheet: ALUres[31:0] = WRITE_ADDRESS; DataB[31:0] = WRITE_DATA;
  //   rd[4:0] = INSTRUCTION2[11:7]; rs1[4:0] = INSTRUCTION2[19:15]; rs2[4:0] = INSTRUCTION2[24:20]

  // Notes on the sheet:
  //   Output to IMEM
  //   IMEM (do **NOT** move this)
  //   Inputs from IMEM
  //   It is OK to move the PC, RegFile, ALU, MEM, Branch Comp, Imm Gen, and Control Logic to wherever is most convenient for you when constructing your CPU, and to delete this text
  //   Inputs/Outputs for testing. Do **NOT** move these.
  //   Outputs To DMEM
  //   DMEM (do **NOT** move this)
  //   Inputs From DMEM
endmodule
